# Fritzing sketch schematic (saved by Fritzing 0.9.2b)
breadboards: 1

parts:
  INA1 = INA219 DC Current Sensor Breakout
  OLED1 = 128x32 I2C Monochrome OLED Display
  J1 = Power Jack [package=power_jack_pth]
  Part2 = Arduino Mega ADK (Rev3)
  IC1 = Voltage Regulator [package=78xxl]
  S1 = Pushbutton [package="[SMD]"]
  M1 = DC Motor

nets:
  VCC: INA1.VCC, OLED1.VIN, Part2.5V, IC1.OUT
  GND: INA1.GND, OLED1.GND, J1.GND, Part2.GND, IC1.GND, S1.Pin_3, S1.Pin_4, M1.pin_1
  N1: INA1.SCL, OLED1.SCL
  N2: INA1.Vin+2, J1.PWR, IC1.IN
  N3: OLED1.RST, Part2.D4_PWM
  N4: Part2.D7_PWM, S1.Pin_1, S1.Pin_2

custom parts:
  INA219 DC Current Sensor Breakout: INA DC Current Sensor Breakout
